// Digital circuit DCC-project2025.dig as structural Verilog
module DCC_project2025 (
  input  [13:0] progIn,
  input  reset,
  input  progLoad,
  input  start,
  input  clk,
  input  [7:0] M,
  input  [7:0] N,
  input  result,
  output valid,
  output [7:0] \output ,
  output done,
  output [3:0] out_12,
  output [7:0] out_13,
  output [7:0] out_14,
  output [3:0] out_15,
  output [15:0] out_16
);

  wire _52, _53, and_1_out, and_2_out, and_3_out, and_4_out, and_5_out, and_6_out, and_8_out, and_23_out,
       comparator_1_eq, comparator_2_eq, comparator_3_eq, comparator_4_eq, comparator_5_eq, comparator_6_eq,
       comparator_7_eq, comparator_8_eq, comparator_9_eq, comparator_10_eq, comparator_11_eq,
       comparator_12_eq, comparator_13_eq, comparator_14_eq, comparator_15_eq, comparator_16_eq,
       comparator_17_eq, comparator_18_eq, comparator_19_eq, comparator_20_eq, comparator_21_eq,
       comparator_22_eq, comparator_23_eq, comparator_24_eq, comparator_25_eq, comparator_26_eq,
       comparator_27_eq, comparator_28_eq, comparator_30_eq, comparator_31_eq, comparator_32_eq,
       comparator_33_eq, comparator_34_eq, comparator_35_eq, comparator_36_eq, comparator_37_eq,
       comparator_38_eq, comparator_39_eq, comparator_40_eq, comparator_41_eq, comparator_42_eq,
       comparator_43_eq, comparator_44_eq, comparator_45_eq, comparator_46_eq, comparator_47_eq,
       comparator_47_gt, comparator_47_lt, comparator_48_eq, comparator_50_eq, comparator_52_eq,
       comparator_53_eq, comparator_54_gt, counter_2_ovf, d_ff_1_q, d_ff_6_q, d_ff_7_q, d_ff_8_q, d_ff_11_q,
       d_ff_12_q, d_ff_13_q, d_ff_15_q, d_ff_16_q, d_ff_17_q, d_ff_19_q, decoder_1_out_3, decoder_2_out_3,
       enA, enB, enC, enD, enflag, enflagAll, equalflag, fact, fact_done, greaterflag, holdreset_for_0_rRAM,
       holdresult, holdstart, lesserflag, load_new_max, load_r_fact, load_r_fact_l, load_r_fact_m, load_sum,
       load_temp, max_done, multiplexer_24_out, multiplexer_33_out, noRemainder, Opcode_51, Opcode_51_delay,
       Opcode_52, Opcode_52_delay, or_1_out, or_2_out, or_3_out, or_4_out, or_5_out, or_6_out, or_7_out,
       or_8_out, or_9_out, or_10_out, or_11_out, or_12_out, or_13_out, or_14_out, or_15_out, or_16_out,
       or_17_out, or_18_out, or_19_out, or_20_out, or_34_out, ovfrRAM, prime, prime_eq, remainder_eq,
       reset_syn, result_syn, rs_ff_as_4_q, select, selectfac, str_Rram, sub_2_c_o;
  wire [1:0] counter_1_out, d_ff_10_q, d_ff_14_q, multiplexer_26_out, multiplexer_27_out, multiplexer_28_out,
       multiplexer_30_out, multiplexer_32_out, prime_2_eq;
  wire [3:0] _1A, counterpreset_2_out, multiplexer_4_out, multiplexer_7_out, multiplexer_12_out,
       multiplexer_14_out, multiplexer_15_out, multiplexer_16_out, multiplexer_17_out, register_1_q,
       register_4_q;
  wire [5:0] Opcode;
  wire [7:0] _1_Din, accA, accA___accB, accA_accB, accA_accB_t, accA_accB_t_t, accA_accB_t_t_t,
       accA_AND_accB, accA_OR_accB, accA_plus_accB, accA_XOR_accB, accB, accC, accD, address_out, data,
       data2, div_1_r, driver_1_out, least_sig_fact, max_num, max_pos, most_sig_fact, multiplexer_1_out,
       multiplexer_2_out, multiplexer_3_out, multiplexer_5_out, multiplexer_6_out, multiplexer_8_out,
       multiplexer_11_out, multiplexer_13_out, multiplexer_18_out, multiplexer_20_out, multiplexer_23_out,
       multiplexer_34_out, NOT_accA, Operand, pRam_adr_operand, prev_q, readaddress, readOperand,
       register_2_q, register_3_q, rotate_left, rotate_right, shift_left, shift_right;
  wire [13:8] pRAM_d1, ramdualport_1_d;
  wire [15:0] d_ff_9_q, mul_3_mul, multiplexer_25_out, multiplexer_29_out, multiplexer_31_out, sub_3_s,
       sum_q, temp_q;
  wire [15:8] mul_2_mul;
  wire [31:16] mul_3_mul_2;

  D_FF d_ff_1 (.D(reset), .C(clk), .Q(d_ff_1_q));  // open: nQ
  or or_1 (or_1_out, start, result_syn);
  D_FF d_ff_2 (.D(reset), .C(clk), .Q(reset_syn));  // open: nQ
  or or_2 (or_2_out, valid, holdresult);
  D_FF d_ff_3 (.D(result), .C(clk), .Q(result_syn));  // open: nQ
  or or_3 (or_3_out, greaterflag, equalflag);
  RS_FF_AS rs_ff_as_1 (.S(d_ff_1_q), .R(or_1_out), .Q(holdreset_for_0_rRAM));  // open: nQ
  or or_4 (or_4_out, greaterflag, lesserflag);
  RS_FF_AS rs_ff_as_2 (.S(result_syn), .R(done), .Q(holdresult));  // open: nQ
  Comparator #(.Bits(6)) comparator_1 (.a(Opcode), .b(6'b010110), .eq(comparator_1_eq));  // open: gt, lt
  Comparator #(.Bits(6)) comparator_2 (.a(Opcode), .b(6'b010111), .eq(comparator_2_eq));  // open: gt, lt
  RS_FF_AS rs_ff_as_3 (.S(start), .R(or_2_out), .Q(holdstart));  // open: nQ
  and and_1 (and_1_out, comparator_1_eq, or_3_out);
  and and_2 (and_2_out, comparator_2_eq, or_4_out);
  Comparator #(.Bits(6)) comparator_3 (.a(Opcode), .b(6'b010011), .eq(comparator_3_eq));  // open: gt, lt
  Comparator #(.Bits(6)) comparator_4 (.a(Opcode), .b(6'b010101), .eq(comparator_4_eq));  // open: gt, lt
  Comparator #(.Bits(6)) comparator_5 (.a(Opcode), .b(6'b010010), .eq(comparator_5_eq));  // open: gt, lt
  Comparator #(.Bits(6)) comparator_6 (.a(Opcode), .b(6'b010100), .eq(comparator_6_eq));  // open: gt, lt
  Counter #(.Bits(8)) address (.en(progLoad), .C(clk), .clr(reset), .out(address_out));  // open: ovf
  and and_3 (and_3_out, comparator_3_eq, equalflag);
  and and_4 (and_4_out, comparator_6_eq, greaterflag);
  and and_5 (and_5_out, comparator_4_eq, lesserflag);
  Multiplexer #(.Bits(8)) multiplexer_1 (
    .sel(load_new_max), .in_0(address_out), .in_1(max_pos), .out(multiplexer_1_out));
  Comparator #(.Bits(6)) comparator_7 (.a(Opcode), .b(6'b000001), .eq(comparator_7_eq));  // open: gt, lt
  Comparator #(.Bits(6)) comparator_8 (.a(Opcode), .b(6'b000011), .eq(comparator_8_eq));  // open: gt, lt
  Comparator #(.Bits(6)) comparator_9 (.a(Opcode), .b(6'b000110), .eq(comparator_9_eq));  // open: gt, lt
  Comparator #(.Bits(6)) comparator_10 (.a(Opcode), .b(6'b001000), .eq(comparator_10_eq));  // open: gt, lt
  Comparator #(.Bits(6)) comparator_11 (.a(Opcode), .b(6'b001110), .eq(comparator_11_eq));  // open: gt, lt
  Comparator #(.Bits(6)) comparator_12 (.a(Opcode), .b(6'b001111), .eq(comparator_12_eq));  // open: gt, lt
  Comparator #(.Bits(6)) comparator_13 (.a(Opcode), .b(6'b010000), .eq(comparator_13_eq));  // open: gt, lt
  Comparator #(.Bits(6)) comparator_14 (.a(Opcode), .b(6'b100000), .eq(comparator_14_eq));  // open: gt, lt
  Comparator #(.Bits(6)) comparator_15 (.a(Opcode), .b(6'b100001), .eq(comparator_15_eq));  // open: gt, lt
  Comparator #(.Bits(6)) comparator_16 (.a(Opcode), .b(6'b100010), .eq(comparator_16_eq));  // open: gt, lt
  Comparator #(.Bits(6)) comparator_17 (.a(Opcode), .b(6'b100011), .eq(comparator_17_eq));  // open: gt, lt
  Comparator #(.Bits(6)) comparator_18 (.a(Opcode), .b(6'b100100), .eq(comparator_18_eq));  // open: gt, lt
  Comparator #(.Bits(6)) comparator_19 (.a(Opcode), .b(6'b100101), .eq(comparator_19_eq));  // open: gt, lt
  Comparator #(.Bits(6)) comparator_20 (.a(Opcode), .b(6'b101000), .eq(comparator_20_eq));  // open: gt, lt
  Comparator #(.Bits(6)) comparator_21 (.a(Opcode), .b(6'b101001), .eq(comparator_21_eq));  // open: gt, lt
  Comparator #(.Bits(6)) comparator_22 (.a(Opcode), .b(6'b101010), .eq(comparator_22_eq));  // open: gt, lt
  Comparator #(.Bits(6)) comparator_23 (.a(Opcode), .b(6'b101011), .eq(comparator_23_eq));  // open: gt, lt
  Comparator #(.Bits(6)) comparator_24 (.a(Opcode), .b(6'b101111), .eq(comparator_24_eq));  // open: gt, lt
  Comparator #(.Bits(6)) comparator_25 (.a(Opcode), .b(6'b101100), .eq(comparator_25_eq));  // open: gt, lt
  Comparator #(.Bits(6)) comparator_26 (.a(Opcode), .b(6'b101101), .eq(comparator_26_eq));  // open: gt, lt
  Comparator #(.Bits(6)) comparator_27 (.a(Opcode), .b(6'b101110), .eq(comparator_27_eq));  // open: gt, lt
  // Probe on multiplexer_1_out
  Multiplexer #(.Bits(8)) multiplexer_2 (
    .sel(progLoad), .in_0(Operand), .in_1(multiplexer_1_out), .out(multiplexer_2_out));
  Comparator #(.Bits(6)) comparator_28 (.a(Opcode), .b(6'b001111), .eq(comparator_28_eq));  // open: gt, lt
  Multiplexer #(.Bits(8)) multiplexer_3 (.sel(or_5_out), .in_0({8{1'b0}}), .in_1(Operand), .out(multiplexer_3_out));
  or or_5 (or_5_out, comparator_5_eq, and_3_out, and_1_out, and_4_out, and_2_out, and_5_out);
  RAMDualAccess #(.AddrBits(8), .Bits(14)) pRAM (
    .str(progLoad), .C(clk), .ld(load_new_max), .A1(multiplexer_1_out), .Din1(progIn), .A2(readaddress),
    .D1({pRAM_d1, readOperand}), .D2({Opcode, Operand}));
  RAMDualPort #(.AddrBits(8), .Bits(14)) ramdualport_1 (
    .A(multiplexer_2_out), .Din(progIn), .str(progLoad), .C(clk), .ld(comparator_28_eq),
    .D({ramdualport_1_d, pRam_adr_operand}));
  and and_6 (and_6_out, holdstart, ~valid);  // And
  or or_6 (or_6_out, reset, start);
  CounterPreset #(.Bits(8)) counterpreset_1 (
    .en(and_6_out), .C(clk), .dir(1'b0), .in(multiplexer_3_out), .ld(or_5_out), .clr(or_6_out),
    .out(readaddress));  // open: ovf
  Comparator #(.Bits(6)) comparator_29 (.a(Opcode), .b({6{1'b1}}), .eq(valid));  // open: gt, lt
  or or_7 (or_7_out, comparator_7_eq, comparator_8_eq, comparator_9_eq, comparator_10_eq, comparator_11_eq, comparator_12_eq, comparator_13_eq, comparator_14_eq, comparator_15_eq, comparator_16_eq, comparator_17_eq, comparator_18_eq, comparator_19_eq, comparator_20_eq, comparator_21_eq, comparator_22_eq, comparator_23_eq, comparator_24_eq, comparator_25_eq, comparator_26_eq, comparator_27_eq);
  // Probe on Operand
  // Probe on Opcode
  // Probe on readaddress
  and and_7 (enA, holdstart, or_7_out);
  and and_8 (and_8_out, holdresult, ~done);  // And
  Comparator #(.Bits(6)) comparator_30 (.a(Opcode), .b(6'b000010), .eq(comparator_30_eq));  // open: gt, lt
  Comparator #(.Bits(6)) comparator_31 (.a(Opcode), .b(6'b000100), .eq(comparator_31_eq));  // open: gt, lt
  Comparator #(.Bits(6)) comparator_32 (.a(Opcode), .b(6'b001110), .eq(comparator_32_eq));  // open: gt, lt
  Comparator #(.Bits(6)) comparator_33 (.a(Opcode), .b(6'b000101), .eq(comparator_33_eq));  // open: gt, lt
  Comparator #(.Bits(6)) comparator_34 (.a(Opcode), .b(6'b001001), .eq(comparator_34_eq));  // open: gt, lt
  Comparator #(.Bits(6)) comparator_35 (.a(Opcode), .b(6'b001010), .eq(comparator_35_eq));  // open: gt, lt
  Comparator #(.Bits(6)) comparator_36 (.a(Opcode), .b(6'b001101), .eq(comparator_36_eq));  // open: gt, lt
  Comparator #(.Bits(6)) comparator_37 (.a(Opcode), .b(6'b000111), .eq(comparator_37_eq));  // open: gt, lt
  Comparator #(.Bits(6)) comparator_38 (.a(Opcode), .b(6'b001011), .eq(comparator_38_eq));  // open: gt, lt
  Comparator #(.Bits(6)) comparator_39 (.a(Opcode), .b(6'b001100), .eq(comparator_39_eq));  // open: gt, lt
  Comparator #(.Bits(6)) comparator_40 (.a(Opcode), .b(6'b001101), .eq(comparator_40_eq));  // open: gt, lt
  CounterPreset #(.Bits(4)) counterpreset_2 (
    .en(and_8_out), .C(clk), .dir(1'b0), .in(4'b0000), .ld(reset_syn), .clr(1'b0), .out(counterpreset_2_out),
    .ovf(ovfrRAM));
  or or_8 (or_8_out, comparator_30_eq, comparator_31_eq, comparator_32_eq);
  or or_9 (or_9_out, comparator_33_eq, comparator_34_eq, comparator_35_eq, comparator_36_eq);
  or or_10 (or_10_out, comparator_37_eq, comparator_38_eq, comparator_39_eq, comparator_40_eq);
  or or_11 (or_11_out, result_syn, reset_syn);
  Multiplexer #(.Bits(4)) multiplexer_4 (
    .sel(comparator_41_eq), .in_0(counterpreset_2_out), .in_1(Operand[3:0]), .out(multiplexer_4_out));
  Comparator #(.Bits(6)) comparator_41 (.a(Opcode), .b(6'b010000), .eq(comparator_41_eq));  // open: gt, lt
  RS_FF_AS rs_ff_as_4 (.S(ovfrRAM), .R(or_11_out), .Q(rs_ff_as_4_q));  // open: nQ
  and and_9 (enB, holdstart, or_8_out);
  Counter #(.Bits(2)) counter_1 (.en(ovfrRAM), .C(clk), .clr(or_11_out), .out(counter_1_out));  // open: ovf
  Comparator #(.Bits(6)) comparator_42 (.a(Opcode), .b(6'b010001), .eq(comparator_42_eq));  // open: gt, lt
  Comparator #(.Bits(6)) comparator_43 (.a(Opcode), .b(6'b001110), .eq(comparator_43_eq));  // open: gt, lt
  Comparator #(.Bits(6)) comparator_44 (.a(Opcode), .b(6'b001101), .eq(comparator_44_eq));  // open: gt, lt
  and and_10 (enC, holdstart, or_9_out);
  and and_11 (enD, holdstart, or_10_out);
  // Probe on counter_1_out
  Comparator #(.Bits(2)) comparator_45 (.a(counter_1_out), .b(2'b01), .eq(comparator_45_eq));  // open: gt, lt
  or or_12 (or_12_out, Opcode_52_delay, Opcode_52);
  or or_13 (or_13_out, Opcode_52_delay, Opcode_52);
  Multiplexer #(.Bits(8)) multiplexer_5 (.sel(comparator_43_eq), .in_0(data), .in_1(data2), .out(multiplexer_5_out));
  Multiplexer #(.Bits(8)) multiplexer_6 (.sel(comparator_44_eq), .in_0(data), .in_1(data2), .out(multiplexer_6_out));
  and and_12 (done, comparator_45_eq, rs_ff_as_4_q);
  or or_14 (or_14_out, holdstart, or_12_out, Opcode_51_delay, max_done);
  or or_15 (or_15_out, holdreset_for_0_rRAM, Opcode_51, max_done, or_13_out, Opcode_51_delay, comparator_42_eq);
  // Probe on data
  Register #(.Bits(8)) u_accA (.D(data), .C(clk), .en(enA), .Q(accA));
  Register #(.Bits(8)) u_accB (.D(multiplexer_5_out), .C(clk), .en(enB), .Q(accB));
  Register #(.Bits(8)) regC (.D(data), .C(clk), .en(enC), .Q(accC));
  Register #(.Bits(8)) regD (.D(multiplexer_6_out), .C(clk), .en(enD), .Q(accD));
  and and_13 (str_Rram, or_14_out, or_15_out);
  Multiplexer #(.Bits(4)) multiplexer_7 (.sel(max_done), .in_0(_1A), .in_1(4'b1001), .out(multiplexer_7_out));
  Multiplexer #(.Bits(8)) multiplexer_8 (.sel(max_done), .in_0(_1_Din), .in_1(max_num), .out(multiplexer_8_out));
  // Probe on accA
  // Probe on accB
  // Probe on accC
  // Probe on accD
  RAMDualAccess #(.AddrBits(4), .Bits(8)) rRAM (
    .str(str_Rram), .C(clk), .ld(1'b0), .A1(multiplexer_7_out), .Din1(multiplexer_8_out),
    .A2(multiplexer_4_out), .D2(\output ));  // open: D1
  // Probe on Operand
  Multiplexer #(.Selector_Bits(6), .Bits(8)) multiplexer_9 (
    .sel(Opcode), .in_0({8{1'b0}}), .in_1(Operand), .in_2(Operand), .in_3(accB), .in_4(accA), .in_5(accA),
    .in_6(accC), .in_7(accA), .in_8(accD), .in_9(M), .in_10(N), .in_11(M), .in_12(N), .in_13(M),
    .in_14(accC), .in_15(pRam_adr_operand), .in_16(\output ), .in_17(accA), .in_18({8{1'b0}}),
    .in_19({8{1'b0}}), .in_20({8{1'b0}}), .in_21({8{1'b0}}), .in_22({8{1'b0}}), .in_23({8{1'b0}}),
    .in_24({8{1'b0}}), .in_25({8{1'b0}}), .in_26({8{1'b0}}), .in_27({8{1'b0}}), .in_28({8{1'b0}}),
    .in_29({8{1'b0}}), .in_30({8{1'b0}}), .in_31({8{1'b0}}), .in_32(accA_plus_accB), .in_33(accA_accB_t_t),
    .in_34(accA_accB_t), .in_35(accA_accB_t_t_t), .in_36(accA_accB), .in_37(accA___accB), .in_38({8{1'b0}}),
    .in_39({8{1'b0}}), .in_40(NOT_accA), .in_41(accA_AND_accB), .in_42(accA_OR_accB), .in_43(accA_XOR_accB),
    .in_44(shift_left), .in_45(rotate_left), .in_46(shift_right), .in_47(rotate_right), .in_48({8{1'b0}}),
    .in_49({8{1'b0}}), .in_50({8{1'b0}}), .in_51({8{1'b0}}), .in_52({8{1'b0}}), .in_53({8{1'b0}}),
    .in_54({8{1'b0}}), .in_55({8{1'b0}}), .in_56({8{1'b0}}), .in_57({8{1'b0}}), .in_58({8{1'b0}}),
    .in_59({8{1'b0}}), .in_60({8{1'b0}}), .in_61({8{1'b0}}), .in_62({8{1'b0}}), .in_63({8{1'b0}}), .out(data));
  Multiplexer #(.Selector_Bits(6), .Bits(8)) multiplexer_10 (
    .sel(Opcode), .in_0({8{1'b0}}), .in_1({8{1'b0}}), .in_2({8{1'b0}}), .in_3({8{1'b0}}), .in_4({8{1'b0}}),
    .in_5({8{1'b0}}), .in_6({8{1'b0}}), .in_7({8{1'b0}}), .in_8({8{1'b0}}), .in_9({8{1'b0}}),
    .in_10({8{1'b0}}), .in_11({8{1'b0}}), .in_12({8{1'b0}}), .in_13(N), .in_14(accD), .in_15({8{1'b0}}),
    .in_16({8{1'b0}}), .in_17({8{1'b0}}), .in_18({8{1'b0}}), .in_19({8{1'b0}}), .in_20({8{1'b0}}),
    .in_21({8{1'b0}}), .in_22({8{1'b0}}), .in_23({8{1'b0}}), .in_24({8{1'b0}}), .in_25({8{1'b0}}),
    .in_26({8{1'b0}}), .in_27({8{1'b0}}), .in_28({8{1'b0}}), .in_29({8{1'b0}}), .in_30({8{1'b0}}),
    .in_31({8{1'b0}}), .in_32({8{1'b0}}), .in_33({8{1'b0}}), .in_34({8{1'b0}}), .in_35({8{1'b0}}),
    .in_36({8{1'b0}}), .in_37({8{1'b0}}), .in_38({8{1'b0}}), .in_39({8{1'b0}}), .in_40({8{1'b0}}),
    .in_41({8{1'b0}}), .in_42({8{1'b0}}), .in_43({8{1'b0}}), .in_44({8{1'b0}}), .in_45({8{1'b0}}),
    .in_46({8{1'b0}}), .in_47({8{1'b0}}), .in_48({8{1'b0}}), .in_49({8{1'b0}}), .in_50({8{1'b0}}),
    .in_51({8{1'b0}}), .in_52({8{1'b0}}), .in_53({8{1'b0}}), .in_54({8{1'b0}}), .in_55({8{1'b0}}),
    .in_56({8{1'b0}}), .in_57({8{1'b0}}), .in_58({8{1'b0}}), .in_59({8{1'b0}}), .in_60({8{1'b0}}),
    .in_61({8{1'b0}}), .in_62({8{1'b0}}), .in_63({8{1'b0}}), .out(data2));
  Seven_Seg_Hex seven_seg_hex_1 (.d(\output [7:4]), .dp(1'b0));
  Seven_Seg_Hex seven_seg_hex_2 (.d(\output [3:0]), .dp(1'b0));
  Comparator #(.Bits(6)) comparator_46 (.a(Opcode), .b(6'b110011), .eq(comparator_46_eq));  // open: gt, lt
  Register #(.Bits(4)) register_1 (.D(Operand[3:0]), .C(clk), .en(Opcode_51), .Q(register_1_q));
  and and_14 (Opcode_51, holdstart, comparator_46_eq);
  Counter #(.Bits(4)) counter_2 (
    .en(holdreset_for_0_rRAM), .C(clk), .clr(or_16_out), .out(out_12), .ovf(counter_2_ovf));
  or or_16 (or_16_out, counter_2_ovf, start);
  Multiplexer #(.Bits(8)) multiplexer_11 (
    .sel(holdreset_for_0_rRAM), .in_0(accA), .in_1({8{1'b0}}), .out(multiplexer_11_out));
  Register #(.Bits(8)) register_2 (.D(out_16[15:8]), .C(clk), .en(Opcode_51), .Q(register_2_q));
  D_FF d_ff_4 (.D(comparator_46_eq), .C(clk), .Q(select));  // open: nQ
  Multiplexer #(.Bits(4)) multiplexer_12 (
    .sel(holdreset_for_0_rRAM), .in_0(Operand[3:0]), .in_1(out_12), .out(multiplexer_12_out));
  Multiplexer #(.Bits(8)) multiplexer_13 (
    .sel(select), .in_0(out_16[7:0]), .in_1(register_2_q), .out(multiplexer_13_out));
  Multiplexer #(.Bits(4)) multiplexer_14 (
    .sel(Opcode_51_delay), .in_0(Operand[3:0]), .in_1(register_1_q), .out(multiplexer_14_out));
  // Probe on register_2_q
  Div #(.Bits(8)) div_1 (.a(accA), .b(accB), .r(div_1_r));  // open: q
  Multiplexer #(.Bits(4)) multiplexer_15 (.sel(select), .in_0(4'b1111), .in_1(4'b1110), .out(multiplexer_15_out));
  Add #(.Bits(8)) add_1 (.a(accA), .b(accB), .c_i(1'b0), .s(accA_plus_accB));  // open: c_o
  Sub #(.Bits(8)) sub_1 (.a(accA), .b(accB), .c_i(1'b0), .s(accA_accB_t_t));  // open: c_o
  Mul #(.Bits(4)) mul_1 (.a(accA[3:0]), .b(accB[3:0]), .mul(accA_accB_t));
  Div #(.Bits(8)) div_2 (.a(accA), .b(accB), .q(accA_accB_t_t_t));  // open: r
  Div #(.Bits(8)) div_3 (.a(accA), .b(accB), .r(accA_accB));  // open: q
  ROM #(.AddrBits(6), .Bits(8)) rom_1 (.A({accA[2:0], accB[2:0]}), .sel(1'b1), .D(accA___accB));
  RAMDualAccess #(.AddrBits(4), .Bits(8)) rRAM_2 (
    .str(str_Rram), .C(clk), .ld(1'b0), .A1(_1A), .Din1(_1_Din), .A2(multiplexer_14_out), .D2(out_13));  // open: D1
  ROM #(.AddrBits(16), .Bits(16)) rom_2 (.A({out_14, out_13}), .sel(1'b1), .D(out_16));
  ROM #(.AddrBits(8)) rom_3 (.A(accA), .sel(1'b1), .D(prime));
  Sub #(.Bits(8)) sub_2 (.a({8{1'b0}}), .b(div_1_r), .c_i(1'b0), .c_o(sub_2_c_o));  // open: s
  Multiplexer #(.Bits(4)) multiplexer_16 (.sel(selectfac), .in_0(4'b1011), .in_1(4'b1010), .out(multiplexer_16_out));
  Register #(.Bits(8)) register_3 (.D(most_sig_fact), .C(clk), .en(Opcode_52), .Q(register_3_q));
  // Probe on out_16
  Register #(.Bits(4)) register_4 (.D(Operand[7:4]), .C(clk), .en(Opcode_51), .Q(register_4_q));
  D_FF d_ff_5 (.D(Opcode_51), .C(clk), .Q(Opcode_51_delay));  // open: nQ
  not not_1 (noRemainder, sub_2_c_o);
  Multiplexer #(.Bits(4)) multiplexer_17 (
    .sel(or_17_out), .in_0(multiplexer_15_out), .in_1(multiplexer_16_out), .out(multiplexer_17_out));
  or or_17 (or_17_out, Opcode_52_delay, Opcode_52);
  Multiplexer #(.Bits(8)) multiplexer_18 (
    .sel(selectfac), .in_0(least_sig_fact), .in_1(register_3_q), .out(multiplexer_18_out));
  // Probe on register_3_q
  Multiplexer #(.Bits(4)) multiplexer_19 (
    .sel(Opcode_51_delay), .in_0(Operand[7:4]), .in_1(register_4_q), .out(out_15));
  Multiplexer #(.Bits(8)) multiplexer_20 (
    .sel(or_18_out), .in_0(multiplexer_13_out), .in_1(multiplexer_18_out), .out(multiplexer_20_out));
  or or_18 (or_18_out, Opcode_52_delay, Opcode_52);
  RAMDualAccess #(.AddrBits(4), .Bits(8)) rRAM_3 (
    .str(str_Rram), .C(clk), .ld(1'b0), .A1(_1A), .Din1(_1_Din), .A2(out_15), .D2(out_14));  // open: D1
  Multiplexer #(.Bits(4)) multiplexer_21 (
    .sel(or_19_out), .in_0(multiplexer_12_out), .in_1(multiplexer_17_out), .out(_1A));
  or or_19 (or_19_out, Opcode_51_delay, Opcode_51, Opcode_52_delay, Opcode_52);
  Multiplexer #(.Bits(8)) multiplexer_22 (
    .sel(or_20_out), .in_0(multiplexer_11_out), .in_1(multiplexer_20_out), .out(_1_Din));
  or or_20 (or_20_out, Opcode_51_delay, Opcode_51, Opcode_52_delay, Opcode_52);
  Comparator #(.Signed("true"), .Bits(8)) comparator_47 (
    .a(accA), .b(accB), .gt(comparator_47_gt), .eq(comparator_47_eq), .lt(comparator_47_lt));
  Comparator #(.Bits(6)) ABcompare (.a(Opcode), .b(6'b110000), .eq(enflagAll));  // open: gt, lt
  Comparator #(.Bits(6)) u_prime (.a(Opcode), .b(6'b110001), .eq(prime_eq));  // open: gt, lt
  Comparator #(.Bits(6)) remainder (.a(Opcode), .b(6'b110010), .eq(remainder_eq));  // open: gt, lt
  Multiplexer #(.Selector_Bits(3), .Bits(8)) multiplexer_23 (
    .sel(accB[2:0]), .in_0(8'h1), .in_1(8'h2), .in_2(8'h4), .in_3(8'h8), .in_4(8'h10), .in_5(8'h20),
    .in_6(8'h40), .in_7(8'h80), .out(multiplexer_23_out));
  Register u_lesserflag (.D(comparator_47_lt), .C(clk), .en(enflagAll), .Q(lesserflag));
  or or_21 (enflag, enflagAll, prime_eq, remainder_eq);
  Mul #(.Bits(8)) mul_2 (.a(accA), .b(multiplexer_23_out), .mul({mul_2_mul, shift_left}));
  Register u_greaterflag (.D(comparator_47_gt), .C(clk), .en(enflagAll), .Q(greaterflag));
  Multiplexer #(.Selector_Bits(2)) multiplexer_24 (
    .sel(prime_2_eq), .in_0(comparator_47_eq), .in_1(prime), .in_2(noRemainder), .in_3(1'b0),
    .out(multiplexer_24_out));
  Comparator #(.Bits(6)) prime_2 (.a(Opcode), .b(6'b110001), .eq(prime_2_eq[0]));  // open: gt, lt
  Comparator #(.Bits(6)) remainder_2 (.a(Opcode), .b(6'b110010), .eq(prime_2_eq[1]));  // open: gt, lt
  Register u_equalflag (.D(multiplexer_24_out), .C(clk), .en(enflag), .Q(equalflag));
  BarrelShifter #(.Bits(8), .direction("right")) barrelshifter_1 (
    .in(accA), .shift({1'b0, accB[2:0]}), .out(shift_right));
  BarrelShifter #(.Bits(8), .barrelShifterMode("rotate")) barrelshifter_2 (
    .in(accA), .shift({1'b0, accB[2:0]}), .out(rotate_left));
  BarrelShifter #(.Bits(8), .barrelShifterMode("rotate"), .direction("right")) barrelshifter_3 (
    .in(accA), .shift({1'b0, accB[2:0]}), .out(rotate_right));
  not not_2 (NOT_accA[0], accA[0]);
  not not_3 (NOT_accA[1], accA[1]);
  not not_4 (NOT_accA[2], accA[2]);
  not not_5 (NOT_accA[3], accA[3]);
  not not_6 (NOT_accA[4], accA[4]);
  not not_7 (NOT_accA[5], accA[5]);
  not not_8 (NOT_accA[6], accA[6]);
  not not_9 (NOT_accA[7], accA[7]);
  Comparator #(.Bits(16)) comparator_48 (
    .a({{13{1'b0}}, accA[2:0]}), .b({16{1'b0}}), .eq(comparator_48_eq));  // open: gt, lt
  Multiplexer #(.Bits(16)) multiplexer_25 (
    .sel(_52), .in_0(sub_3_s), .in_1({{13{1'b0}}, accA[2:0]}), .out(multiplexer_25_out));
  Comparator #(.Bits(6)) comparator_49 (.a(Opcode), .b(6'b110100), .eq(_52));  // open: gt, lt
  D_FF d_ff_6 (.D(_52), .C(clk), .Q(d_ff_6_q));  // open: nQ
  Sub #(.Bits(16)) sub_3 (.a(temp_q), .b(16'h1), .c_i(1'b0), .s(sub_3_s));  // open: c_o
  Multiplexer #(.Bits(2)) multiplexer_26 (.sel(fact_done), .in_0(2'b01), .in_1(2'b11), .out(multiplexer_26_out));
  Multiplexer #(.Bits(2)) multiplexer_27 (.sel(decoder_2_out_3), .in_0(2'b11), .in_1(2'b00), .out(multiplexer_27_out));
  Comparator #(.Bits(6)) comparator_50 (.a(Opcode), .b(6'b110100), .eq(comparator_50_eq));  // open: gt, lt
  Comparator #(.Bits(6)) comparator_51 (.a(Opcode), .b(6'b110101), .eq(_53));  // open: gt, lt
  and and_15 (accA_AND_accB[0], accA[0], accB[0]);
  and and_16 (accA_AND_accB[1], accA[1], accB[1]);
  and and_17 (accA_AND_accB[2], accA[2], accB[2]);
  and and_18 (accA_AND_accB[3], accA[3], accB[3]);
  and and_19 (accA_AND_accB[4], accA[4], accB[4]);
  and and_20 (accA_AND_accB[5], accA[5], accB[5]);
  and and_21 (accA_AND_accB[6], accA[6], accB[6]);
  and and_22 (accA_AND_accB[7], accA[7], accB[7]);
  Register #(.Bits(16)) temp (.D(multiplexer_25_out), .C(clk), .en(load_temp), .Q(temp_q));
  Comparator #(.Bits(16)) comparator_52 (.a(sub_3_s), .b(16'h1), .eq(comparator_52_eq));  // open: gt, lt
  or or_22 (load_temp, fact, _52);
  Multiplexer #(.Selector_Bits(2), .Bits(2)) multiplexer_28 (
    .sel(d_ff_10_q), .in_0({_52, 1'b0}), .in_1(2'b10), .in_2(multiplexer_26_out), .in_3(multiplexer_27_out),
    .out(multiplexer_28_out));
  D_FF d_ff_7 (.D(comparator_50_eq), .C(clk), .Q(d_ff_7_q));  // open: nQ
  CounterPreset #(.Bits(8)) counterpreset_3 (
    .en(load_new_max), .C(clk), .dir(1'b0), .in(accA), .ld(_53), .clr(and_23_out), .out(max_pos));  // open: ovf
  D_FF d_ff_8 (.D(and_23_out), .C(clk), .Q(d_ff_8_q));  // open: nQ
  Multiplexer #(.Bits(16)) multiplexer_29 (.sel(d_ff_6_q), .in_0(mul_3_mul), .in_1(temp_q), .out(multiplexer_29_out));
  D_FF #(.Bits(16)) d_ff_9 (.D(sub_3_s), .C(clk), .Q(d_ff_9_q));  // open: nQ
  or or_23 (fact_done, comparator_48_eq, comparator_52_eq);
  D_FF #(.Bits(2)) d_ff_10 (.D(multiplexer_28_out), .C(clk), .Q(d_ff_10_q));  // open: nQ
  D_FF d_ff_11 (.D(d_ff_7_q), .C(clk), .Q(d_ff_11_q));  // open: nQ
  Mul #(.Bits(16)) mul_3 (.a(sum_q), .b(d_ff_9_q), .mul({mul_3_mul_2, mul_3_mul}));
  // Probe on readOperand
  assign driver_1_out = load_new_max ? readOperand : 8'bz;  // Driver driver_1
  Comparator #(.Signed("true"), .Bits(8)) comparator_53 (.a(max_pos), .b(accB), .eq(comparator_53_eq));  // open: gt, lt
  and and_23 (and_23_out, comparator_53_eq, load_new_max);
  or or_24 (max_done, and_23_out, d_ff_8_q);
  Register #(.Bits(16)) sum (.D(multiplexer_29_out), .C(clk), .en(load_sum), .Q(sum_q));
  Decoder #(.Selector_Bits(2)) decoder_1 (
    .sel(d_ff_10_q), .out_1(fact), .out_2(load_sum), .out_3(decoder_1_out_3));  // open: out_0
  Multiplexer #(.Bits(2)) multiplexer_30 (.sel(reset), .in_0(2'b11), .in_1(2'b00), .out(multiplexer_30_out));
  D_FF d_ff_12 (.D(d_ff_11_q), .C(clk), .Q(d_ff_12_q));  // open: nQ
  // Probe on max_pos
  // Probe on max_done
  or or_25 (accA_OR_accB[0], accA[0], accB[0]);
  or or_26 (accA_OR_accB[1], accA[1], accB[1]);
  or or_27 (accA_OR_accB[2], accA[2], accB[2]);
  or or_28 (accA_OR_accB[3], accA[3], accB[3]);
  or or_29 (accA_OR_accB[4], accA[4], accB[4]);
  or or_30 (accA_OR_accB[5], accA[5], accB[5]);
  or or_31 (accA_OR_accB[6], accA[6], accB[6]);
  or or_32 (accA_OR_accB[7], accA[7], accB[7]);
  Multiplexer #(.Bits(16)) multiplexer_31 (
    .sel(comparator_48_eq), .in_0(mul_3_mul), .in_1(16'h1), .out(multiplexer_31_out));
  assign {most_sig_fact, least_sig_fact} = fact_done ? multiplexer_31_out : 16'bz;  // Driver driver_2
  // Probe on {most_sig_fact, least_sig_fact}
  or or_33 (load_r_fact, decoder_1_out_3, multiplexer_33_out);
  D_FF d_ff_13 (.D(d_ff_12_q), .C(clk), .Q(d_ff_13_q));  // open: nQ
  Register #(.Bits(8)) prev (.D(driver_1_out), .C(clk), .en(comparator_54_gt), .Q(prev_q));
  Multiplexer #(.Selector_Bits(2), .Bits(2)) multiplexer_32 (
    .sel(d_ff_14_q), .in_0({1'b0, load_r_fact}), .in_1(2'b10), .in_2(2'b11), .in_3(multiplexer_30_out),
    .out(multiplexer_32_out));
  D_FF #(.Bits(2)) d_ff_14 (.D(multiplexer_32_out), .C(clk), .Q(d_ff_14_q));  // open: nQ
  D_FF d_ff_15 (.D(d_ff_13_q), .C(clk), .Q(d_ff_15_q));  // open: nQ
  Multiplexer multiplexer_33 (.sel(_52), .in_0(1'b0), .in_1(comparator_48_eq), .out(multiplexer_33_out));
  Multiplexer #(.Bits(8)) multiplexer_34 (.sel(_53), .in_0(prev_q), .in_1({8{1'b0}}), .out(multiplexer_34_out));
  or or_34 (or_34_out, _53, max_done);
  xor xor_1 (accA_XOR_accB[0], accA[0], accB[0]);
  xor xor_2 (accA_XOR_accB[1], accA[1], accB[1]);
  xor xor_3 (accA_XOR_accB[2], accA[2], accB[2]);
  xor xor_4 (accA_XOR_accB[3], accA[3], accB[3]);
  xor xor_5 (accA_XOR_accB[4], accA[4], accB[4]);
  xor xor_6 (accA_XOR_accB[5], accA[5], accB[5]);
  xor xor_7 (accA_XOR_accB[6], accA[6], accB[6]);
  xor xor_8 (accA_XOR_accB[7], accA[7], accB[7]);
  Decoder #(.Selector_Bits(2)) decoder_2 (
    .sel(d_ff_14_q), .out_1(load_r_fact_l), .out_2(load_r_fact_m), .out_3(decoder_2_out_3));  // open: out_0
  D_FF d_ff_16 (.D(d_ff_15_q), .C(clk), .Q(d_ff_16_q));  // open: nQ
  Register register_5 (.D(_53), .C(clk), .en(or_34_out), .Q(load_new_max));
  D_FF d_ff_17 (.D(d_ff_16_q), .C(clk), .Q(d_ff_17_q));  // open: nQ
  Comparator #(.Signed("true"), .Bits(8)) comparator_54 (
    .a(driver_1_out), .b(max_num), .gt(comparator_54_gt));  // open: eq, lt
  D_FF #(.Bits(8)) d_ff_18 (.D(multiplexer_34_out), .C(clk), .Q(max_num));  // open: nQ
  D_FF d_ff_19 (.D(d_ff_17_q), .C(clk), .Q(d_ff_19_q));  // open: nQ
  D_FF d_ff_20 (.D(d_ff_19_q), .C(clk), .Q(Opcode_52));  // open: nQ
  // Probe on max_num
  D_FF d_ff_21 (.D(Opcode_52), .C(clk), .Q(selectfac));  // open: nQ
  D_FF d_ff_22 (.D(Opcode_52), .C(clk), .Q(Opcode_52_delay));  // open: nQ

  // Other names for the same wires on the sheet: accA_0 = accA[0]; accA_1 = accA[1]; accA_2 = accA[2];
  //   accA_3 = accA[3]; accA_4 = accA[4]; accA_5 = accA[5]; accA_6 = accA[6]; accA_7 = accA[7]; accB_0 = accB[0];
  //   accB_1 = accB[1]; accB_2 = accB[2]; accB_3 = accB[3]; accB_4 = accB[4]; accB_5 = accB[5]; accB_6 = accB[6];
  //   accB_7 = accB[7]; fact_t = _52; LCM[15:0] = out_16; least_sig_LCM[7:0] = out_16[7:0];
  //   most_sig_LCM[7:0] = out_16[15:8]; rRAm___m[7:0] = out_13; rRAm___n[7:0] = out_14;
  //   rRAM_adr_Operand[7:0] = \output ; stop = valid

  // Notes on the sheet:
  //   CU
  //   6833032521
  //   Jesadakorn Netthong
  //   6833042821
  //   Chonchanok Srisongkram
  //   6833071021
  //   Napat Putsorn
  //   6833098021
  //   Thaweechai Petchkwan
  //   Register
  //   ALU
  //   + - * / % ^
  //   contents of rom_1 (hex, n*v repeats v):
  //   1,7*0,9*1,2,4,8,10,20,40,80,1,3,9,1b,51,f3,d9,8b,1,4,10,40,100
  //   ,400,1000,4000,1,5,19,7d,71,35,9,2d,1,6,24,d8,510,80,10,44580
  //   ,1,7,31,157,961,41a7,1cb91,c90f7
  //   contents of rom_2 (hex, n*v repeats v):
  //   257*0,1,2,3,4,5,6,7,8,9,a,b,c,d,e,f,10,11,12,13,14,15,16,17,18
  //   ,19,1a,1b,1c,1d,1e,1f,20,21,22,23,24,25,26,27,28,29,2a,2b,2c,2d
  //   ,2e,2f,30,31,32,33,34,35,36,37,38,39,3a,3b,3c,3d,3e,3f,40,41,42
  //   ,43,44,45,46,47,48,49,4a,4b,4c,4d,4e,4f,50,51,52,53,54,55,56,57
  //   ,58,59,5a,5b,5c,5d,5e,5f,60,61,62,63,64,65,66,67,68,69,6a,6b,6c
  //   ,6d,6e,6f,70,71,72,73,74,75,76,77,78,79,7a,7b,7c,7d,7e,7f,80,81
  //   ,82,83,84,85,86,87,88,89,8a,8b,8c,8d,8e,8f,90,91,92,93,94,95,96
  //   ,97,98,99,9a,9b,9c,9d,9e,9f,a0,a1,a2,a3,a4,a5,a6,a7,a8,a9,aa,ab
  //   ,ac,ad,ae,af,b0,b1,b2,b3,b4,b5,b6,b7,b8,b9,ba,bb,bc,bd,be,bf,c0
  //   ,c1,c2,c3,c4,c5,c6,c7,c8,c9,ca,cb,cc,cd,ce,cf,d0,d1,d2,d3,d4,d5
  //   ,d6,d7,d8,d9,da,db,dc,dd,de,df,e0,e1,e2,e3,e4,e5,e6,e7,e8,e9,ea
  //   ,eb,ec,ed,ee,ef,f0,f1,f2,f3,f4,f5,f6,f7,f8,f9,fa,fb,fc,fd,fe,ff
  //   ,0,2,2,6,4,a,6,e,8,12,a,16,c,1a,e,1e,10,22,12,26,14,2a,16,2e,18
  //   ,32,1a,36,1c,3a,1e,3e,20,42,22,46,24,4a,26,4e,28,52,2a,56,2c,5a
  //   ,2e,5e,30,62,32,66,34,6a,36,6e,38,72,3a,76,3c,7a,3e,7e,40,82,42
  //   ,86,44,8a,46,8e,48,92,4a,96,4c,9a,4e,9e,50,a2,52,a6,54,aa,56,ae
  //   ,58,b2,5a,b6,5c,ba,5e,be,60,c2,62,c6,64,ca,66,ce,68,d2,6a,d6,6c
  //   ,da,6e,de,70,e2,72,e6,74,ea,76,ee,78,f2,7a,f6,7c,fa,7e,fe,80,102
  //   ,82,106,84,10a,86,10e,88,112,8a,116,8c,11a,8e,11e,90,122,92,126
  //   ,94,12a,96,12e,98,132,9a,136,9c,13a,9e,13e,a0,142,a2,146,a4,14a
  //   ,a6,14e,a8,152,aa,156,ac,15a,ae,15e,b0,162,b2,166,b4,16a,b6,16e
  //   ,b8,172,ba,176,bc,17a,be,17e,c0,182,c2,186,c4,18a,c6,18e,c8,192
  //   ,ca,196,cc,19a,ce,19e,d0,1a2,d2,1a6,d4,1aa,d6,1ae,d8,1b2,da,1b6
  //   ,dc,1ba,de,1be,e0,1c2,e2,1c6,e4,1ca,e6,1ce,e8,1d2,ea,1d6,ec,1da
  //   ,ee,1de,f0,1e2,f2,1e6,f4,1ea,f6,1ee,f8,1f2,fa,1f6,fc,1fa,fe,1fe
  //   ,0,3,6,3,c,f,6,15,18,9,1e,21,c,27,2a,f,30,33,12,39,3c,15,42,45
  //   ,18,4b,4e,1b,54,57,1e,5d,60,21,66,69,24,6f,72,27,78,7b,2a,81,84
  //   ,2d,8a,8d,30,93,96,33,9c,9f,36,a5,a8,39,ae,b1,3c,b7,ba,3f,c0,c3
  //   ,42,c9,cc,45,d2,d5,48,db,de,4b,e4,e7,4e,ed,f0,51,f6,f9,54,ff,102
  //   ,57,108,10b,5a,111,114,5d,11a,11d,60,123,126,63,12c,12f,66,135
  //   ,138,69,13e,141,6c,147,14a,6f,150,153,72,159,15c,75,162,165,78
  //   ,16b,16e,7b,174,177,7e,17d,180,81,186,189,84,18f,192,87,198,19b
  //   ,8a,1a1,1a4,8d,1aa,1ad,90,1b3,1b6,93,1bc,1bf,96,1c5,1c8,99,1ce
  //   ,1d1,9c,1d7,1da,9f,1e0,1e3,a2,1e9,1ec,a5,1f2,1f5,a8,1fb,1fe,ab
  //   ,204,207,ae,20d,210,b1,216,219,b4,21f,222,b7,228,22b,ba,231,234
  //   ,bd,23a,23d,c0,243,246,c3,24c,24f,c6,255,258,c9,25e,261,cc,267
  //   ,26a,cf,270,273,d2,279,27c,d5,282,285,d8,28b,28e,db,294,297,de
  //   ,29d,2a0,e1,2a6,2a9,e4,2af,2b2,e7,2b8,2bb,ea,2c1,2c4,ed,2ca,2cd
  //   ,f0,2d3,2d6,f3,2dc,2df,f6,2e5,2e8,f9,2ee,2f1,fc,2f7,2fa,ff,0,4,4
  //   ,c,4,14,c,1c,8,24,14,2c,c,34,1c,3c,10,44,24,4c,14,54,2c,5c,18
  //   ,64,34,6c,1c,74,3c,7c,20,84,44,8c,24,94,4c,9c,28,a4,54,ac,2c,b4
  //   ,5c,bc,30,c4,64,cc,34,d4,6c,dc,38,e4,74,ec,3c,f4,7c,fc,40,104
  //   ,84,10c,44,114,8c,11c,48,124,94,12c,4c,134,9c,13c,50,144,a4,14c
  //   ,54,154,ac,15c,58,164,b4,16c,5c,174,bc,17c,60,184,c4,18c,64,194
  //   ,cc,19c,68,1a4,d4,1ac,6c,1b4,dc,1bc,70,1c4,e4,1cc,74,1d4,ec,1dc
  //   ,78,1e4,f4,1ec,7c,1f4,fc,1fc,80,204,104,20c,84,214,10c,21c,88
  //   ,224,114,22c,8c,234,11c,23c,90,244,124,24c,94,254,12c,25c,98,264
  //   ,134,26c,9c,274,13c,27c,a0,284,144,28c,a4,294,14c,29c,a8,2a4,154
  //   ,2ac,ac,2b4,15c,2bc,b0,2c4,164,2cc,b4,2d4,16c,2dc,b8,2e4,174,2ec
  //   ,bc,2f4,17c,2fc,c0,304,184,30c,c4,314,18c,31c,c8,324,194,32c,cc
  //   ,334,19c,33c,d0,344,1a4,34c,d4,354,1ac,35c,d8,364,1b4,36c,dc,374
  //   ,1bc,37c,e0,384,1c4,38c,e4,394,1cc,39c,e8,3a4,1d4,3ac,ec,3b4,1dc
  //   ,3bc,f0,3c4,1e4,3cc,f4,3d4,1ec,3dc,f8,3e4,1f4,3ec,fc,3f4,1fc,3fc
  //   ,0,5,a,f,14,5,1e,23,28,2d,a,37,3c,41,46,f,50,55,5a,5f,14,69,6e
  //   ,73,78,19,82,87,8c,91,1e,9b,a0,a5,aa,23,b4,b9,be,c3,28,cd,d2,d7
  //   ,dc,2d,e6,eb,f0,f5,32,ff,104,109,10e,37,118,11d,122,127,3c,131
  //   ,136,13b,140,41,14a,14f,154,159,46,163,168,16d,172,4b,17c,181
  //   ,186,18b,50,195,19a,19f,1a4,55,1ae,1b3,1b8,1bd,5a,1c7,1cc,1d1
  //   ,1d6,5f,1e0,1e5,1ea,1ef,64,1f9,1fe,203,208,69,212,217,21c,221
  //   ,6e,22b,230,235,23a,73,244,249,24e,253,78,25d,262,267,26c,7d,276
  //   ,27b,280,285,82,28f,294,299,29e,87,2a8,2ad,2b2,2b7,8c,2c1,2c6
  //   ,2cb,2d0,91,2da,2df,2e4,2e9,96,2f3,2f8,2fd,302,9b,30c,311,316
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  //   contents of rom_3 (hex, n*v repeats v):
  //   0,a,1,1,0,1,a,1,0,0,a,1,0,1,0,0,a,1,a,1,0,0,0,1,a,0,0,50,0,1,0
  //   ,1,5*0,1,0,50,0,1,0,1,0,90,0,1,a,50,a,0,0,1,0,50,0,70,0,1,0,1
  //   ,5*0,1,0,0,0,1,0,1,0,150,0,0,0,1,0,0,0,1,0,70,0,0,0,1,5*0,70,0
  //   ,1,0,0,0,1,0,1,0,110,0,1,0,1,0,0,0,1,0,0,0,50,0,110,0,50,0,0,0
  //   ,110,0,1,0,0,0,1,5*0,1,0,1,9*0,1,0,1,5*0,1,5*0,1,0,0,0,1,5*0,1
  //   ,5*0,1,0,1,9*0,1,0,1,0,0,0,1,0,1,11*0,1,11*0,1,15*0,1,0,1,9*0,1
  //   flag&compare
  //   shift&rotate
  //   Factorial
endmodule

/* Test case 23_P07T03:
M N progIn reset progLoad start result clk valid done output
0 0      0     0        0     0      0   0     x    x      x
0 0      0     0        0     0      0   1     x    x      x
0 0      0     1        0     0      0   0     x    x      x
0 0      0     1        0     0      0   1     0    0      x
0 0      0     0        0     0      0   0     0    0      x
0 0      0     0        0     0      0   1     0    0      x
0 0      0     0        0     0      0   0     0    0      x
0 0      0     0        0     0      0   1     0    0      x
0 0      0     0        0     0      0   0     0    0      x
0 0      0     0        0     0      0   1     0    0      x
0 0      0     0        0     0      0   0     0    0      x
0 0      0     0        0     0      0   1     0    0      x
0 0      0     0        0     0      0   0     0    0      x
0 0      0     0        0     0      0   1     0    0      x
0 0      0     0        0     0      0   0     0    0      x
0 0      0     0        0     0      0   1     0    0      x
0 0      0     0        0     0      0   0     0    0      x
0 0      0     0        0     0      0   1     0    0      x
0 0      0     0        0     0      0   0     0    0      x
0 0      0     0        0     0      0   1     0    0      x
0 0      0     0        0     0      0   0     0    0      x
0 0      0     0        0     0      0   1     0    0      x
0 0      0     0        0     0      0   0     0    0      x
0 0      0     0        0     0      0   1     0    0      x
0 0      0     0        0     0      0   0     0    0      x
0 0      0     0        0     0      0   1     0    0      x
0 0      0     0        0     0      0   0     0    0      x
0 0      0     0        0     0      0   1     0    0      x
0 0      0     0        0     0      0   0     0    0      x
0 0      0     0        0     0      0   1     0    0      x
0 0      0     0        0     0      0   0     0    0      x
0 0      0     0        0     0      0   1     0    0      x
0 0      0     0        0     0      0   0     0    0      x
0 0      0     0        0     0      0   1     0    0      x
0 0      0     0        0     0      0   0     0    0      x
0 0      0     0        0     0      0   1     0    0      x
0 0      0     0        0     0      0   0     0    0      x
0 0      0     0        0     0      0   1     0    0      x
0 0      0     0        0     0      0   0     0    0      x
0 0      0     0        0     0      0   1     0    0      x
0 0      0     0        0     0      0   0     0    0      x
0 0      0     0        0     0      0   1     0    0      x
0 0      0     0        0     0      0   0     0    0      x
0 0      0     0        0     0      0   1     0    0      x
0 0    306     0        1     0      0   0     0    0      x
0 0    306     0        1     0      0   1     0    0      x
0 0   4352     0        1     0      0   0     0    0      x
0 0   4352     0        1     0      0   1     0    0      x
0 0    366     0        1     0      0   0     0    0      x
0 0    366     0        1     0      0   1     0    0      x
0 0   4357     0        1     0      0   0     0    0      x
0 0   4357     0        1     0      0   1     0    0      x
0 0  13136     0        1     0      0   0     0    0      x
0 0  13136     0        1     0      0   1     0    0      x
0 0  16128     0        1     0      0   0     0    0      x
0 0  16128     0        1     0      0   1     0    0      x
0 0      0     0        0     0      0   0     0    0      x
0 0      0     0        0     0      0   1     0    0      x
0 0      0     0        0     1      0   0     0    0      x
0 0      0     0        0     1      0   1     0    0      x
0 0      0     0        0     0      0   0     x    0      x
0 0      0     0        0     0      0   1     x    0      x
0 0      0     0        0     0      0   0     x    0      x
0 0      0     0        0     0      0   1     x    0      x
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*/

/* Test case 29_P11T2:
M N progIn reset progLoad start result clk valid done output
0 0      0     0        0     0      0   0     x    x      x
0 0      0     0        0     0      0   1     x    x      x
0 0      0     1        0     0      0   0     x    x      x
0 0      0     1        0     0      0   1     0    0      x
0 0      0     0        0     0      0   0     0    0      x
0 0      0     0        0     0      0   1     0    0      x
0 0      0     0        0     0      0   0     0    0      x
0 0      0     0        0     0      0   1     0    0      x
0 0      0     0        0     0      0   0     0    0      x
0 0      0     0        0     0      0   1     0    0      x
0 0      0     0        0     0      0   0     0    0      x
0 0      0     0        0     0      0   1     0    0      x
0 0      0     0        0     0      0   0     0    0      x
0 0      0     0        0     0      0   1     0    0      x
0 0      0     0        0     0      0   0     0    0      x
0 0      0     0        0     0      0   1     0    0      x
0 0      0     0        0     0      0   0     0    0      x
0 0      0     0        0     0      0   1     0    0      x
0 0      0     0        0     0      0   0     0    0      x
0 0      0     0        0     0      0   1     0    0      x
0 0      0     0        0     0      0   0     0    0      x
0 0      0     0        0     0      0   1     0    0      x
0 0      0     0        0     0      0   0     0    0      x
0 0      0     0        0     0      0   1     0    0      x
0 0      0     0        0     0      0   0     0    0      x
0 0      0     0        0     0      0   1     0    0      x
0 0      0     0        0     0      0   0     0    0      x
0 0      0     0        0     0      0   1     0    0      x
0 0      0     0        0     0      0   0     0    0      x
0 0      0     0        0     0      0   1     0    0      x
0 0      0     0        0     0      0   0     0    0      x
0 0      0     0        0     0      0   1     0    0      x
0 0      0     0        0     0      0   0     0    0      x
0 0      0     0        0     0      0   1     0    0      x
0 0      0     0        0     0      0   0     0    0      x
0 0      0     0        0     0      0   1     0    0      x
0 0      0     0        0     0      0   0     0    0      x
0 0      0     0        0     0      0   1     0    0      x
0 0      0     0        0     0      0   0     0    0      x
0 0      0     0        0     0      0   1     0    0      x
0 0      0     0        0     0      0   0     0    0      x
0 0      0     0        0     0      0   1     0    0      x
0 0      0     0        0     0      0   0     0    0      x
0 0      0     0        0     0      0   1     0    0      x
0 0     27     0        1     0      0   0     0    0      x
0 0     27     0        1     0      0   1     0    0      x
0 0     60     0        1     0      0   0     0    0      x
0 0     60     0        1     0      0   1     0    0      x
0 0     30     0        1     0      0   0     0    0      x
0 0     30     0        1     0      0   1     0    0      x
0 0    255     0        1     0      0   0     0    0      x
0 0    255     0        1     0      0   1     0    0      x
0 0      6     0        1     0      0   0     0    0      x
0 0      6     0        1     0      0   1     0    0      x
0 0    251     0        1     0      0   0     0    0      x
0 0    251     0        1     0      0   1     0    0      x
0 0    127     0        1     0      0   0     0    0      x
0 0    127     0        1     0      0   1     0    0      x
0 0    120     0        1     0      0   0     0    0      x
0 0    120     0        1     0      0   1     0    0      x
0 0    232     0        1     0      0   0     0    0      x
0 0    232     0        1     0      0   1     0    0      x
0 0      0     0        1     0      0   0     0    0      x
0 0      0     0        1     0      0   1     0    0      x
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*/

/* Test case 28_P11T01:
M N progIn reset progLoad start result clk valid done output
0 0      0     0        0     0      0   0     x    x      x
0 0      0     0        0     0      0   1     x    x      x
0 0      0     1        0     0      0   0     x    x      x
0 0      0     1        0     0      0   1     0    0      x
0 0      0     0        0     0      0   0     0    0      x
0 0      0     0        0     0      0   1     0    0      x
0 0      0     0        0     0      0   0     0    0      x
0 0      0     0        0     0      0   1     0    0      x
0 0      0     0        0     0      0   0     0    0      x
0 0      0     0        0     0      0   1     0    0      x
0 0      0     0        0     0      0   0     0    0      x
0 0      0     0        0     0      0   1     0    0      x
0 0      0     0        0     0      0   0     0    0      x
0 0      0     0        0     0      0   1     0    0      x
0 0      0     0        0     0      0   0     0    0      x
0 0      0     0        0     0      0   1     0    0      x
0 0      0     0        0     0      0   0     0    0      x
0 0      0     0        0     0      0   1     0    0      x
0 0      0     0        0     0      0   0     0    0      x
0 0      0     0        0     0      0   1     0    0      x
0 0      0     0        0     0      0   0     0    0      x
0 0      0     0        0     0      0   1     0    0      x
0 0      0     0        0     0      0   0     0    0      x
0 0      0     0        0     0      0   1     0    0      x
0 0      0     0        0     0      0   0     0    0      x
0 0      0     0        0     0      0   1     0    0      x
0 0      0     0        0     0      0   0     0    0      x
0 0      0     0        0     0      0   1     0    0      x
0 0      0     0        0     0      0   0     0    0      x
0 0      0     0        0     0      0   1     0    0      x
0 0      0     0        0     0      0   0     0    0      x
0 0      0     0        0     0      0   1     0    0      x
0 0      0     0        0     0      0   0     0    0      x
0 0      0     0        0     0      0   1     0    0      x
0 0      0     0        0     0      0   0     0    0      x
0 0      0     0        0     0      0   1     0    0      x
0 0      0     0        0     0      0   0     0    0      x
0 0      0     0        0     0      0   1     0    0      x
0 0      0     0        0     0      0   0     0    0      x
0 0      0     0        0     0      0   1     0    0      x
0 0      0     0        0     0      0   0     0    0      x
0 0      0     0        0     0      0   1     0    0      x
0 0      0     0        0     0      0   0     0    0      x
0 0      0     0        0     0      0   1     0    0      x
0 0     27     0        1     0      0   0     0    0      x
0 0     27     0        1     0      0   1     0    0      x
0 0     60     0        1     0      0   0     0    0      x
0 0     60     0        1     0      0   1     0    0      x
0 0     30     0        1     0      0   0     0    0      x
0 0     30     0        1     0      0   1     0    0      x
0 0    255     0        1     0      0   0     0    0      x
0 0    255     0        1     0      0   1     0    0      x
0 0      6     0        1     0      0   0     0    0      x
0 0      6     0        1     0      0   1     0    0      x
0 0    251     0        1     0      0   0     0    0      x
0 0    251     0        1     0      0   1     0    0      x
0 0    127     0        1     0      0   0     0    0      x
0 0    127     0        1     0      0   1     0    0      x
0 0    120     0        1     0      0   0     0    0      x
0 0    120     0        1     0      0   1     0    0      x
0 0    232     0        1     0      0   0     0    0      x
0 0    232     0        1     0      0   1     0    0      x
0 0      0     0        1     0      0   0     0    0      x
0 0      0     0        1     0      0   1     0    0      x
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*/

/* Test case 05_P03T02:
M N progIn reset progLoad start result clk valid done output
0 0      0     0        0     0      0   0     x    x      x
0 0      0     0        0     0      0   1     x    x      x
0 0      0     1        0     0      0   0     x    x      x
0 0      0     1        0     0      0   1     0    0      x
0 0      0     0        0     0      0   0     0    0      x
0 0      0     0        0     0      0   1     0    0      x
0 0      0     0        0     0      0   0     0    0      x
0 0      0     0        0     0      0   1     0    0      x
0 0      0     0        0     0      0   0     0    0      x
0 0      0     0        0     0      0   1     0    0      x
0 0      0     0        0     0      0   0     0    0      x
0 0      0     0        0     0      0   1     0    0      x
0 0      0     0        0     0      0   0     0    0      x
0 0      0     0        0     0      0   1     0    0      x
0 0      0     0        0     0      0   0     0    0      x
0 0      0     0        0     0      0   1     0    0      x
0 0      0     0        0     0      0   0     0    0      x
0 0      0     0        0     0      0   1     0    0      x
0 0      0     0        0     0      0   0     0    0      x
0 0      0     0        0     0      0   1     0    0      x
0 0      0     0        0     0      0   0     0    0      x
0 0      0     0        0     0      0   1     0    0      x
0 0      0     0        0     0      0   0     0    0      x
0 0      0     0        0     0      0   1     0    0      x
0 0      0     0        0     0      0   0     0    0      x
0 0      0     0        0     0      0   1     0    0      x
0 0      0     0        0     0      0   0     0    0      x
0 0      0     0        0     0      0   1     0    0      x
0 0      0     0        0     0      0   0     0    0      x
0 0      0     0        0     0      0   1     0    0      x
0 0      0     0        0     0      0   0     0    0      x
0 0      0     0        0     0      0   1     0    0      x
0 0      0     0        0     0      0   0     0    0      x
0 0      0     0        0     0      0   1     0    0      x
0 0      0     0        0     0      0   0     0    0      x
0 0      0     0        0     0      0   1     0    0      x
0 0      0     0        0     0      0   0     0    0      x
0 0      0     0        0     0      0   1     0    0      x
0 0      0     0        0     0      0   0     0    0      x
0 0      0     0        0     0      0   1     0    0      x
0 0      0     0        0     0      0   0     0    0      x
0 0      0     0        0     0      0   1     0    0      x
0 0      0     0        0     0      0   0     0    0      x
0 0      0     0        0     0      0   1     0    0      x
0 0    296     0        1     0      0   0     0    0      x
0 0    296     0        1     0      0   1     0    0      x
0 0    527     0        1     0      0   0     0    0      x
0 0    527     0        1     0      0   1     0    0      x
0 0   3846     0        1     0      0   0     0    0      x
0 0   3846     0        1     0      0   1     0    0      x
0 0   8192     0        1     0      0   0     0    0      x
0 0   8192     0        1     0      0   1     0    0      x
0 0   4361     0        1     0      0   0     0    0      x
0 0   4361     0        1     0      0   1     0    0      x
0 0   3847     0        1     0      0   0     0    0      x
0 0   3847     0        1     0      0   1     0    0      x
0 0   8206     0        1     0      0   0     0    0      x
0 0   8206     0        1     0      0   1     0    0      x
0 0     36     0        1     0      0   0     0    0      x
0 0     36     0        1     0      0   1     0    0      x
0 0   8199     0        1     0      0   0     0    0      x
0 0   8199     0        1     0      0   1     0    0      x
0 0   4357     0        1     0      0   0     0    0      x
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*/

/* Test case 12_P08T01:
M N progIn reset progLoad start result clk valid done output
0 0      0     0        0     0      0   0     x    x      x
0 0      0     0        0     0      0   1     x    x      x
0 0      0     1        0     0      0   0     x    x      x
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*/

/* Test case 06_P04T01:
M N progIn reset progLoad start result clk valid done output
0 0      0     0        0     0      0   0     x    x      x
0 0      0     0        0     0      0   1     x    x      x
0 0      0     1        0     0      0   0     x    x      x
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*/

/* Test case 13_P08T02:
M N progIn reset progLoad start result clk valid done output
0 0      0     0        0     0      0   0     x    x      x
0 0      0     0        0     0      0   1     x    x      x
0 0      0     1        0     0      0   0     x    x      x
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*/

/* Test case 24_P08T03:
M N progIn reset progLoad start result clk valid done output
0 0      0     0        0     0      0   0     x    x      x
0 0      0     0        0     0      0   1     x    x      x
0 0      0     1        0     0      0   0     x    x      x
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*/

/* Test case 26_P10T01:
M N progIn reset progLoad start result clk valid done output
0 0      0     0        0     0      0   0     x    x      x
0 0      0     0        0     0      0   1     x    x      x
0 0      0     1        0     0      0   0     x    x      x
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*/

/* Test case 07_P05T01:
M N progIn reset progLoad start result clk valid done output
0 0      0     0        0     0      0   0     x    x      x
0 0      0     0        0     0      0   1     x    x      x
0 0      0     1        0     0      0   0     x    x      x
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*/
